# Fritzing sketch TractorBot (saved by Fritzing 0.9.2b)
stripboards: 1

parts:
  IC1 = L293D [package=THT]
  J1 = shrouded pin header, 40 pins [form="♂ (shrouded male)"]
  IC2 = Voltage Regulator [package=78xxl]
  J2 = double row male pin header, 2 pins [form="♂ (male)"]
  LED1 = LED - 5mm [color="Red (633nm)" package="5 mm [THT]"]
  LED2 = LED - 5mm [color="Green (570nm)" package="5 mm [THT]"]
  S1 = Pushbutton [package="[THT]"]
  S2 = Pushbutton [package="[THT]"]
  J6 = screw terminal, 4 pins
  J7 = screw terminal, 4 pins
  J8 = screw terminal, 2 pins
  J10 = male pin header, 3 pins [form="♂ (male)"]
  J9 = male pin header, 3 pins [form="♂ (male)"]
  J11 = male pin header, 3 pins [form="♂ (male)"]
  M1 = DC Motor
  M2 = DC Motor
  M3 = DC Motor
  M4 = DC Motor
  VCC1 = 4 x AAA Battery Mount
  R1 = Resistor [tolerance=±5% resistance=220 package=THT]
  C1 = Electrolytic Capacitor [capacitance=22µF package="100 mil [THT, electrolytic]"]
  C2 = Ceramic Capacitor [capacitance=100nF package="1206 [SMD, multilayer]"]
  R2 = Resistor [tolerance=±5% resistance=220 package=THT]
  J13 = male pin header, 7 pins [form="♂ (male)"]
  J12 = male pin header, 5 pins [form="♂ (male)"]
  J14 = male pin header, 3 pins [form="♂ (male)"]

nets:
  N1: IC1.Enable_1, J1.pin21, J1.pin35, J12.pin3
  N2: IC1.In_1, J1.pin30
  N3: IC1.Out_1_(_Controlled_by_Enable_1_), J7.pin1, J7.pin3, M3.pin_2, M4.pin_2
  N4: IC1.0V, J1.pin18, IC2.GND, LED1.cathode, LED2.cathode, S1.Pin_1, S1.Pin_2, S2.Pin_3, S2.Pin_4, J8.pin2, J10.pin1, J9.pin1, J11.pin3, VCC1.-, C1.-, C2.0, J13.pin1, J12.pin1, J14.pin1
  N5: IC1.Out_2_(_Controlled_by_Enable_1_), J7.pin2, J7.pin4, M3.pin_1, M4.pin_1
  N6: IC1.In_2, J1.pin31
  N7: IC1.+Vmotor, IC2.IN, J8.pin1, VCC1.+, C2.1
  N8: IC1.In_3, J1.pin8
  N9: IC1.Out_3_(_Controlled_by_Enable_2_), J6.pin2, J6.pin4, M1.pin_1, M2.pin_1
  N10: IC1.Out_4_(_Controlled_by_Enable_2_), J6.pin1, J6.pin3, M1.pin_2, M2.pin_2
  N11: IC1.In_4, J1.pin9
  N12: IC1.+V, J1.pin20, J2.pin2
  N13: J1.pin10, R2.Pin_0
  N14: J1.pin12, S2.Pin_1, S2.Pin_2
  N15: J1.pin13, R1.Pin_0
  N16: J1.pin15, S1.Pin_3, S1.Pin_4
  N17: J1.pin16, J11.pin1
  N18: J1.pin17, J11.pin2
  N19: J1.pin24, J10.pin3
  N20: J1.pin26, J9.pin3
  N21: J1.pin27, J12.pin4
  N22: J1.pin28, J12.pin5
  N23: J1.pin32, J14.pin3
  N24: J1.pin36, J13.pin4
  N25: J1.pin37, J13.pin5
  N26: J1.pin38, J13.pin6
  N27: J1.pin39, J13.pin7
  N28: IC2.OUT, J2.pin1, J10.pin2, J9.pin2, C1.+, J13.pin2, J12.pin2, J14.pin2
  N29: LED1.anode, R2.Pin_1
  N30: LED2.anode, R1.Pin_1

notes:
  Right Motors
  Left Motors
